# Fritzing sketch switch transistor (saved by Fritzing 0.7.12b)
breadboards: 1

parts:
  Arduino1 = Arduino
  Q1 = NPN-Transistor [package="TO92 [THT]"]
  R1 = Resistor [tolerance=±5% resistance=220 package=THT]
  LED1 = LED - 5mm [color="Red (633nm)" package="5 mm [THT]"]

nets:
  N1: Arduino1.GND, LED1.cathode
  N2: Arduino1.D13, R1.Pin_1
  N3: Arduino1.+5V, Q1.C
  N4: Q1.E, LED1.anode
  N5: Q1.B, R1.Pin_0

notes:
  piano/teclado
  tecla piano
